// Logisim project beta2.circ as structural Verilog: 1 circuit, main circuit main
module main (
  input  J1Pedra,
  input  J1Papel,
  input  J1Tesoura,
  input  J2Pedra,
  input  J2Papel,
  input  J2Tesoura,
  output J1V,
  output Empate,
  output J2V
);

  wire and_1_out, and_2_out, and_3_out, and_4_out, and_5_out, and_6_out, not_1_out, not_2_out;

  and and_1 (and_1_out, J1Pedra, J2Tesoura);
  and and_2 (and_2_out, J1Papel, J2Pedra);
  and and_3 (and_3_out, J1Tesoura, J2Papel);
  and and_4 (and_4_out, J1Tesoura, J2Pedra);
  and and_5 (and_5_out, J1Pedra, J2Papel);
  and and_6 (and_6_out, J1Papel, J2Tesoura);
  or or_1 (J1V, and_1_out, and_2_out, and_3_out);
  or or_2 (J2V, and_4_out, and_5_out, and_6_out);
  not not_1 (not_1_out, J1V);
  not not_2 (not_2_out, J2V);
  and and_7 (Empate, not_1_out, not_2_out);
endmodule
