// Logisim project beta3.circ as structural Verilog: 1 circuit, main circuit main
module main (
  input  J1Pedra,
  input  J1Papel,
  input  J1Tesoura,
  input  J2Pedra,
  input  J2Papel,
  input  J2Tesoura,
  output Empate,
  output J1V,
  output J2V
);

  wire and_1_out, and_2_out, and_3_out, and_4_out, and_5_out, and_6_out, and_7_out, and_8_out, and_9_out;

  and and_1 (and_1_out, J1Papel, J2Papel);
  and and_2 (and_2_out, J1Pedra, J2Pedra);
  and and_3 (and_3_out, J1Tesoura, J2Tesoura);
  or or_1 (Empate, and_2_out, and_1_out, and_3_out);
  and and_4 (and_4_out, J1Pedra, J2Tesoura);
  and and_5 (and_5_out, J1Papel, J2Pedra);
  and and_6 (and_6_out, J1Tesoura, J2Papel);
  and and_7 (and_7_out, J1Tesoura, J2Pedra);
  and and_8 (and_8_out, J1Pedra, J2Papel);
  and and_9 (and_9_out, J1Papel, J2Tesoura);
  or or_2 (J1V, and_4_out, and_5_out, and_6_out);
  or or_3 (J2V, and_7_out, and_8_out, and_9_out);

  // Notes on the sheet:
  //   JOGO JOKENPO!
endmodule
