// Logisim project rpsgame.circ as structural Verilog: 1 circuit, main circuit main
module main (
  input  J1Pedra,
  input  J1Papel,
  input  J1Tesoura,
  input  J2Pedra,
  input  J2Papel,
  input  J2Tesoura,
  output Empate,
  output J1V,
  output J2V,
  output Erro
);

  wire and_1_out, and_2_out, and_3_out, and_4_out, and_5_out, and_6_out, and_7_out, and_8_out, and_9_out,
       and_10_out, and_11_out, and_12_out, and_13_out, and_14_out, and_15_out;

  and and_1 (and_1_out, J1Pedra, J1Tesoura);
  and and_2 (and_2_out, J1Pedra, J1Papel);
  and and_3 (and_3_out, J1Tesoura, J1Papel);
  and and_4 (and_4_out, J1Papel, J2Papel);
  and and_5 (and_5_out, J1Pedra, J2Pedra);
  or or_1 (Erro, and_2_out, and_1_out, and_3_out, and_8_out, and_7_out, and_9_out);
  and and_6 (and_6_out, J1Tesoura, J2Tesoura);
  and and_7 (and_7_out, J2Pedra, J2Tesoura);
  and and_8 (and_8_out, J2Tesoura, J2Papel);
  or or_2 (Empate, and_5_out, and_4_out, and_6_out);
  and and_9 (and_9_out, J2Tesoura, J2Papel);
  and and_10 (and_10_out, J1Pedra, J2Tesoura);
  and and_11 (and_11_out, J1Papel, J2Pedra);
  and and_12 (and_12_out, J1Tesoura, J2Papel);
  and and_13 (and_13_out, J1Tesoura, J2Pedra);
  and and_14 (and_14_out, J1Pedra, J2Papel);
  and and_15 (and_15_out, J1Papel, J2Tesoura);
  or or_3 (J1V, and_10_out, and_11_out, and_12_out);
  or or_4 (J2V, and_13_out, and_14_out, and_15_out);

  // Notes on the sheet:
  //   JOGO JOKENPO!
endmodule
